# Fritzing sketch derdiedas_diagram (saved by Fritzing 0.9.3b)
breadboards: 1

parts:
  Part1 = Arduino Uno (Rev3)
  S1 = Pushbutton [package="[THT]"]
  S2 = Pushbutton [package="[THT]"]
  S3 = Pushbutton [package="[THT]"]
  LCD1 = LCD screen  # not connected
  R2 = Resistor [tolerance=±5% resistance=220 package="2010 [SMD]"]
  R3 = Resistor [tolerance=±5% resistance=220 package="1206 [SMD]"]
  R4 = Resistor [tolerance=±5% resistance=220 package="1206 [SMD]"]

nets:
  N1: Part1.D5_PWM, S1.Pin_3, S1.Pin_4, R2.Pin_1
  N2: Part1.D6_PWM, S2.Pin_3, S2.Pin_4, R3.Pin_1
  N3: Part1.D7, S3.Pin_3, S3.Pin_4, R4.Pin_1
  N4: Part1.5V, S1.Pin_1, S1.Pin_2, S2.Pin_1, S2.Pin_2, S3.Pin_1, S3.Pin_2
  N5: Part1.GND, R2.Pin_0, R3.Pin_0, R4.Pin_0
